# Fritzing sketch Remote Control Stripboard (saved by Fritzing 1.0.2b)
stripboards: 1

parts:
  Part2 = Adafruit Analog 2-Axis Joystick [part_number="Adafruit #512"]
  R1 = Rotary Potentiometer (Small) [maximum_resistance=10kΩ knob_status=50% power=0.5W package=THT]
  R2 = Resistor [tolerance=±5% resistance=10k package="1206 [SMD]"]
  Part3 = Arduino Uno (Rev3) - ICSP
  Part4 = NRF24L01+ Breakout Board
  VCC1 = Battery block 9V
  R3 = Resistor [tolerance=±5% resistance=220 package="2010 [SMD]"]
  LED1 = LED - 3mm [color="Red (633nm)" current=0.030A package="3 mm [THT]"]

nets:
  GND: Part2.GND, R1.leg2, Part3.GND, Part4.GND, VCC1.-, R3.Pin_0
  N1: Part2.SWITCH, R2.Pin_1, Part3.D2
  N2: Part2.YOUT, Part3.A3
  N3: Part2.XOUT, Part3.A5/SCL
  VCC: Part2.VCC, R1.leg1, R2.Pin_0, Part3.5V
  N4: R1.wiper, Part3.A1
  N5: Part3.D8, Part4.CS
  N6: Part3.D9_PWM, Part4.CE
  N7: Part3.D11_PWM/MOSI, Part4.MOSI
  N8: Part3.D12/MISO, Part4.MISO
  N9: Part3.D13/SCK, Part4.SCK
  N10: Part3.D7, LED1.anode
  3V3: Part3.3V3, Part4.VCC
  N11: Part3.VIN, VCC1.+
  N12: R3.Pin_1, LED1.cathode

custom parts:
  Adafruit Analog 2-Axis Joystick: This mini-kit makes it easy to mount a PSP/Xbox-like thumb joystick to your project. The thumbstick is an analog joystick - more accurate and sensitive than just 'directional' joysticks - with a 'press in to select' button. Since it's analog, you'll need two analog reading pins on your microcontroller to determine X and Y. Having an extra digital input will let you read the switch. The pack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
